# Fritzing sketch WiringPurwarupa (saved by Fritzing 0.9.5d)

parts:
  A1 = Wemos S2 Mini [part_number="WeMos D1 Mini Lite"]
  TP1 = TP4056 [chip_label=TP4056 package="DIP (Dual Inline) [THT]"]
  A2 = mini boost module
  S1 = Pushbutton [package="[THT]"]
  OLED_I2C1 = OLED 128x64 I2C Monochrome Display
  S2 = Toggle Switch [package=THT]
  VCC1 = Battery
  J2 = top view banana jack black [package=THT]
  J3 = top view banana jack red [package=THT]
  J1 = top view banana jack red [package=THT]
  INA1 = INA219 DC Current Sensor Breakout
  SW1 = DIP SWITCH [package=dipswitch-02]
  R1 = Resistor [tolerance=±5% resistance=200 package="0402 [SMD]"]
  R2 = Resistor [tolerance=±5% resistance=100 package="0402 [SMD]"]
  R3 = Resistor [tolerance=±5% resistance=100k package="0402 [SMD]"]
  R4 = Resistor [tolerance=±5% resistance=15k package="0402 [SMD]"]
  R5 = Resistor [tolerance=±5% resistance=1k package="0402 [SMD]"]  # not connected

nets:
  N1: A1.Pin_7, SW1.1
  VDD: A1.Pin_17, A2.Pin_4, OLED_I2C1.VDD, INA1.VCC
  GND: A1.Pin_18, A1.Pin_26, A2.Pin_3, S1.Pin_3, S1.Pin_4, OLED_I2C1.GND, J2.pin1, INA1.GND, INA1.Vin-2, SW1.4, R4.Pin_0
  N2: A1.Pin_21, OLED_I2C1.SDA, INA1.SDA
  N3: A1.Pin_22, OLED_I2C1.SCK, INA1.SCL
  N4: A1.Pin_23, S1.Pin_2
  N5: A1.Pin_25, R1.Pin_1, R2.Pin_0
  N6: A1.Pin_27, R3.Pin_0
  N7: TP1.pin3, S2.L1
  N8: TP1.pin4, VCC1.+, R1.Pin_0
  N9: TP1.pin5, VCC1.-, R2.Pin_1
  N10: TP1.pin6, A2.Pin_1
  N11: A2.Pin_2, S2.COM
  N12: J3.pin1, R3.Pin_1
  N13: J1.pin1, INA1.Vin+2

notes:
  Voltage
  Current

custom parts:
  Wemos S2 Mini: A mini wifi board based on the ESP32-S2FN4R2.
  TP4056: A DIP stand-in part for whatever IC you want. With 6 pins on a 300mil dual inline package (DIP) footprint.
  mini boost module: mini boost module.
  Battery: Your standard 2x 18650 battery pack (7,4 Volts)
  top view banana jack black: Top view banana jack black.
  top view banana jack red: Top view banana jack red.
  INA219 DC Current Sensor Breakout: INA DC Current Sensor Breakout
